# Fritzing sketch Dr-Ajectory_Wiring_Schematic (saved by Fritzing 0.9.3b)

parts:
  Bauteil1 = Arduino Nano (Rev3.0)
  S1 = Round Pushbutton
  J1 = Basic Servo
  J2 = Infrared Proximity Sensor
  LED1 = 7-SEGMENT-4DIGIT-YOUNGSUN [package=7-segment-4digit-youngsun-longpads]
  LED2 = LED - 3mm [color="Red (633nm)" package="3 mm [THT]"]
  VCC1 = Battery block 9V
  S2 = Toggle Switch [package=THT]
  R1 = Resistor [tolerance=±5% resistance=220 package=THT]
  R2 = Resistor [tolerance=±5% resistance=220 package=THT]
  R3 = Resistor [tolerance=±5% resistance=220 package=THT]

nets:
  N1: Bauteil1.D1/TX, J2.Vout
  N2: Bauteil1.D2, LED2.cathode
  N3: Bauteil1.D3, LED1.DIG3
  N4: Bauteil1.D4, LED1.E
  N5: Bauteil1.D5, LED1.D
  N6: Bauteil1.D6, LED1.DIG2
  N7: Bauteil1.D7, LED1.APOS-A
  N8: Bauteil1.D8, LED1.C
  N9: Bauteil1.D9, LED1.A
  N10: Bauteil1.D10, R1.Pin_0
  N11: Bauteil1.D11/MOSI, R3.Pin_0
  N12: Bauteil1.D12/MISO, R2.Pin_0
  N13: Bauteil1.VIN, S2.COM
  N14: Bauteil1.A0, S1.leg1
  N15: Bauteil1.D13/SCK, J1.pulse
  N16: LED1.DP, R1.Pin_1
  N17: LED1.F, R3.Pin_1
  N18: LED1.COL-C, R2.Pin_1
  N19: VCC1.-, S2.L2
  N20: VCC1.+, S2.L1

notes:
  Laserdiode
  7-Segment Display
  Laser Rangefinder
  Servo Motor
  Pushbutton
  9V Battery
  3-Pin Slide Switch
  1K Ohm Resistors
